// Digital circuit 4bit-addierer.dig as structural Verilog
module _4bit_addierer (
  input  A3,
  input  A2,
  input  A1,
  input  A0,
  input  B3,
  input  B2,
  input  B1,
  input  B0,
  output S0,
  output S1,
  output S2,
  output S3
);

  wire undriven;

  LED C0 (.in(undriven));

  // Notes on the sheet:
  //   Zahl 1
  //   Zahl 2
  //   Ergebnis
  //   Überlauf
endmodule

/* Test case:
            A3 A2 A1 A0  B3 B2 B1 B0 C0 S3 S2 S1 S0
repeat(256) bits(4,n>>4) bits(4,n)   bits(5,(n>>4)+(n&15))
*/
