// Digital circuit xor.dig as structural Verilog
module \xor  (
  input  A,
  input  B,
  output Y
);

  // Or or_1 is placed but not wired
  // And and_1 is placed but not wired
  // And and_2 is placed but not wired
  // Not not_1 is placed but not wired
  // Not not_2 is placed but not wired
endmodule

/* Test case:
A  B   Y
0  0   0
1  0   1
0  1   1
1  1   0
*/
