// Digital circuit xor2.dig as structural Verilog
module xor2 (
  input  i1,
  input  i2,
  output o1
);

  wire and_1_out, not_1_out, or_1_out;

  and and_1 (and_1_out, i1, i2);
  or or_1 (or_1_out, i1, i2);
  not not_1 (not_1_out, and_1_out);
  and and_2 (o1, or_1_out, not_1_out);
endmodule

/* Test case:
i1 i2  o1
0  0   0
1  0   1
0  1   1
1  1   0
*/
