// Digital circuit grundgatter_nand.dig as structural Verilog
module grundgatter_nand (
  input  A,
  input  B,
  output NOT,
  output AND,
  output out_5
);

  wire nand_2_out, nand_3_out, nand_4_out;

  nand nand_1 (NOT, A, A);
  nand nand_2 (nand_2_out, A, B);
  nand nand_3 (nand_3_out, A, A);
  nand nand_4 (nand_4_out, B, B);
  nand nand_5 (AND, nand_2_out, nand_2_out);
  nand nand_6 (out_5, nand_3_out, nand_4_out);
endmodule
