// Digital circuit beispiel1.dig as structural Verilog
module beispiel1 (
  input  s_0,
  input  s_1,
  input  s_2,
  input  s_3,
  input  s_4,
  input  s_5,
  input  s_6
);

  Seven_Seg seven_seg_1 (.a(s_0), .b(s_1), .c(s_2), .d(s_3), .e(s_4), .f(s_5), .g(s_6), .dp(1'b0));
endmodule
