// Digital circuit digiConv2.dig as structural Verilog
module digiConv2 (
  input  A,
  input  B,
  input  C,
  output Y,
  output X,
  output W,
  output V,
  output U,
  output T,
  output S,
  output R
);

  wire and_1_out, and_2_out, and_3_out, and_4_out, not_1_out, not_2_out, not_3_out;

  not not_1 (not_1_out, A);
  not not_2 (not_2_out, B);
  not not_3 (not_3_out, C);
  and and_1 (and_1_out, not_2_out, not_3_out);
  and and_2 (and_2_out, not_2_out, not_3_out);
  and and_3 (and_3_out, not_2_out, not_3_out);
  and and_4 (and_4_out, not_2_out, not_3_out);
  or or_1 (Y, not_1_out, and_1_out);
  or or_2 (V, not_1_out, and_2_out);
  or or_3 (U, not_1_out, and_3_out);
  or or_4 (T, not_1_out, and_4_out);

  assign R = 1'b0;
  assign S = 1'b0;
  assign W = 1'b1;
  assign X = 1'b1;
endmodule
