// Digital circuit 4bit-addierer.dig as structural Verilog
module _4bit_addierer (
  input  A3,
  input  A2,
  input  A1,
  input  A0,
  input  B3,
  input  B2,
  input  B1,
  input  B0,
  output S0,
  output S1,
  output S2,
  output S3
);

  wire halbaddierer_1_co, volladdierer_1_co, volladdierer_2_co, volladdierer_3_co;

  halbaddierer halbaddierer_1 (.A(A0), .B(B0), .S(S0), .Co(halbaddierer_1_co));
  volladdierer volladdierer_1 (.A(A1), .B(B1), .Ci(halbaddierer_1_co), .S(S1), .Co(volladdierer_1_co));
  volladdierer volladdierer_2 (.A(A2), .B(B2), .Ci(volladdierer_1_co), .S(S2), .Co(volladdierer_2_co));
  volladdierer volladdierer_3 (.A(A3), .B(B3), .Ci(volladdierer_2_co), .S(S3), .Co(volladdierer_3_co));
  LED C0 (.in(volladdierer_3_co));

  // Notes on the sheet:
  //   Zahl 1
  //   Zahl 2
  //   Ergebnis
  //   Überlauf
endmodule

/* Test case:
            A3 A2 A1 A0  B3 B2 B1 B0 C0 S3 S2 S1 S0
repeat(256) bits(4,n>>4) bits(4,n)   bits(5,(n>>4)+(n&15))
*/
