// Digital circuit digital.dig as structural Verilog
module digital (
  input  in_1,
  input  in_2,
  input  in_3,
  input  in_4
);

  wire digiconv2_1_r, digiconv2_1_s, digiconv2_1_t, digiconv2_1_u, digiconv2_1_v, digiconv2_1_w,
       digiconv2_1_x, digiconv2_1_y, digiconv_1_r, digiconv_1_s, digiconv_1_t, digiconv_1_u, digiconv_1_v,
       digiconv_1_w, digiconv_1_x, digiconv_1_y;

  digiConv digiconv_1 (
    .A(in_1), .B(in_2), .C(in_3), .D(in_4), .Y(digiconv_1_y), .X(digiconv_1_x), .W(digiconv_1_w),
    .V(digiconv_1_v), .U(digiconv_1_u), .T(digiconv_1_t), .S(digiconv_1_s), .R(digiconv_1_r));
  digiConv2 digiconv2_1 (
    .A(in_1), .B(in_2), .C(in_3), .Y(digiconv2_1_y), .X(digiconv2_1_x), .W(digiconv2_1_w), .V(digiconv2_1_v),
    .U(digiconv2_1_u), .T(digiconv2_1_t), .S(digiconv2_1_s), .R(digiconv2_1_r));
  Seven_Seg seven_seg_1 (
    .a(digiconv2_1_y), .b(digiconv2_1_x), .c(digiconv2_1_w), .d(digiconv2_1_v), .e(digiconv2_1_u),
    .f(digiconv2_1_t), .g(digiconv2_1_s), .dp(digiconv2_1_r));
  Seven_Seg seven_seg_2 (
    .a(digiconv_1_y), .b(digiconv_1_x), .c(digiconv_1_w), .d(digiconv_1_v), .e(digiconv_1_u),
    .f(digiconv_1_t), .g(digiconv_1_s), .dp(digiconv_1_r));
endmodule
