// Digital circuit halbaddierer.dig as structural Verilog
module halbaddierer (
  input  A,
  input  B,
  output S,
  output Co
);

  \xor  xor_1 (.A(A), .B(B), .Y(S));
  and and_1 (Co, A, B);
endmodule

/* Test case:
A B    S Co
0 0    0 0
1 0    1 0
0 1    1 0
1 1    0 1
*/
