// Digital circuit volladdierer.dig as structural Verilog
module volladdierer (
  input  A,
  input  B,
  input  Ci,
  output S,
  output Co
);

  wire halbaddierer_1_co, halbaddierer_1_s, halbaddierer_2_co;

  halbaddierer halbaddierer_1 (.A(A), .B(B), .S(halbaddierer_1_s), .Co(halbaddierer_1_co));
  halbaddierer halbaddierer_2 (.A(halbaddierer_1_s), .B(Ci), .S(S), .Co(halbaddierer_2_co));
  or or_1 (Co, halbaddierer_1_co, halbaddierer_2_co);
endmodule

/* Test case:
A B Ci    S Co
0 0 0     0 0
0 1 0     1 0
1 0 0     1 0
1 1 0     0 1
0 0 1     1 0
0 1 1     0 1
1 0 1     0 1
1 1 1     1 1
*/
