// Digital circuit grundgatter.dig as structural Verilog
module grundgatter (
  input  A,
  input  B,
  input  C,
  output Y
);

  wire and_1_out, or_1_out;

  or or_1 (or_1_out, A, and_1_out);
  and and_1 (and_1_out, B, C);
  not not_1 (Y, or_1_out);
endmodule

/* Test case:
 A B C Y 

 0 0 0 0
 0 0 1 0
 0 1 0 1
 0 1 1 0
 1 0 0 1
 1 0 1 0
 1 1 0 1
 1 1 1 0
*/
